# Fritzing sketch SketchSemaforo (saved by Fritzing 0.9.3b)
breadboards: 1

parts:
  Componente1 = Arduino Uno (Rev3)
  R1 = Resistor [tolerance=±5% resistance=1k package="0402 [SMD]"]
  S1 = Pushbutton [package=THT]
  R2 = Rotary Potentiometer (Small) [maximum_resistance=100kΩ package=THT]
  LED6 = smd LED [color="Green (555nm)" package="0603 [SMD]"]
  LED7 = smd LED [color="Yellow (592nm)" package="0603 [SMD]"]
  LED8 = smd LED [color="Red (633nm)" package="0603 [SMD]"]
  LED9 = smd LED [color="Green (555nm)" package="0603 [SMD]"]
  LED10 = smd LED [color="Red (633nm)" package="0603 [SMD]"]

nets:
  N1: Componente1.A0, R2.wiper
  N2: Componente1.D8, LED10.anode
  N3: Componente1.D9_PWM, LED9.anode
  N4: Componente1.D10_PWM/SS, LED8.anode
  N5: Componente1.D11_PWM/MOSI, LED7.anode
  N6: Componente1.D12/MISO, LED6.anode
  N7: Componente1.D2, R1.Pin_0, S1.leg1
  N8: Componente1.5V, R1.Pin_1, R2.leg2
  N9: Componente1.GND, S1.leg0, R2.leg1, LED6.cathode, LED7.cathode, LED8.cathode, LED9.cathode, LED10.cathode
